# Fritzing sketch tanqueolas (saved by Fritzing 0.8.7b)
breadboards: 1

parts:
  Parte1 = Arduino Uno (Rev3)
  C1 = Ceramic Capacitor [capacitance=100nF package="1206 [SMD, multilayer]"]
  R1 = Resistor [tolerance=±5% resistance=4.7k package="1206 [SMD]"]
  R3 = Resistor [tolerance=±5% resistance=220 package="1206 [SMD]"]
  R2 = Resistor [tolerance=±5% resistance=220 package="1206 [SMD]"]
  R5 = Resistor [tolerance=±5% resistance=220 package="1206 [SMD]"]
  R4 = Resistor [tolerance=±5% resistance=220 package="1206 [SMD]"]
  J3 = female pin header, 5 pins [form="♀ (female)"]
  J1 = female pin header, 3 pins [form="♀ (female)"]
  J2 = female pin header, 3 pins [form="♀ (female)"]

nets:
  N1: Parte1.A0, R3.Pin_1, R2.Pin_0, J3.pin3
  N2: Parte1.A1, R5.Pin_0, J3.pin2, J2.pin3
  N3: Parte1.A2, R4.Pin_0, J3.pin1, J2.pin2
  GND: Parte1.GND, C1.0, R3.Pin_0, R5.Pin_1, R4.Pin_1, J3.pin5, J1.pin3, J2.pin1
  N4: Parte1.D3_PWM, R1.Pin_1
  N5: C1.1, R1.Pin_0, J3.pin4, J1.pin2
  N6: R2.Pin_1, J1.pin1

notes:
  consigna
  posición
  h1
  h2
